# Fritzing sketch Transistor (saved by Fritzing 0.9.2b)
breadboards: 1

parts:
  Part1 = Arduino Micro (Rev3)  # not connected
  Q1 = Basic FET P-Channel [package="TO220 [THT]"]
  VCC1 = 4 x AAA Battery Mount
  M1 = DC Motor
  D1 = Rectifier Diode [part_number=1N4001 package="300 mil [THT]"]

nets:
  N1: Q1.drain, VCC1.+
  N2: Q1.source, D1.cathode
  N3: M1.pin_1, D1.anode

notes:
  BD243B
